# Fritzing sketch modulo_controle (saved by Fritzing 0.9.3b)
breadboards: 1

parts:
  ARDUINO = Arduino Uno (Rev3)
  MODULO_SD = MicroSD Card Module
  CASA_1 = RJ45 Jack [package=rj45-8]
  CASA_2 = RJ45 Jack [package=rj45-8]
  CASA_3 = RJ45 Jack [package=rj45-8]
  RTC = Real Time Clock Module - DS1307 RTC Breakout Board

nets:
  N1: ARDUINO.A1, CASA_1.5
  N2: ARDUINO.A2, CASA_2.5
  N3: ARDUINO.A3, CASA_3.5
  N4: ARDUINO.A4/SDA, RTC.SDA
  N5: ARDUINO.A5/SCL, RTC.SCL
  N6: ARDUINO.D10_PWM/SS, MODULO_SD.CS
  N7: ARDUINO.D11_PWM/MOSI, MODULO_SD.MOSI
  N8: ARDUINO.D12/MISO, MODULO_SD.MISO
  N9: ARDUINO.D13/SCK, MODULO_SD.SCK
  N10: ARDUINO.D2, CASA_1.2
  N11: ARDUINO.D3_PWM, CASA_1.3
  N12: ARDUINO.D4, CASA_2.2
  N13: ARDUINO.D5_PWM, CASA_2.3
  N14: ARDUINO.D6_PWM, CASA_3.2
  N15: ARDUINO.D7, CASA_3.3
  5V: ARDUINO.5V, MODULO_SD.VCC, CASA_1.1, CASA_2.1, CASA_3.1, RTC.5V
  GND: ARDUINO.GND, MODULO_SD.GND, CASA_1.7, CASA_1.8, CASA_2.7, CASA_2.8, CASA_3.7, CASA_3.8, RTC.GND
